# Fritzing sketch Bass Couch (saved by Fritzing 0.8.0b)
breadboards: 2

parts:
  Q2 = npn-Powertransistor [part_number=TIP120 package="TO220 [THT]"]
  D1 = Rectifier Diode [part_number=1N4001 package="300 mil [THT]"]
  LED1 = LED - 3mm [color="Blue (430nm)" package="3 mm [THT]"]
  Part1 = Arduino Uno (Rev3)
  R1 = Resistor [tolerance=±5% resistance=220 package="0805 [SMD]"]
  C1 = Electrolytic Capacitor [capacitance=0.1mF package="100 mil [THT, electrolytic]"]
  Power_plug1 = Power plug
  LED2 = LED - 3mm [color="Blue (430nm)" package="3 mm [THT]"]
  LED3 = LED - 3mm [color="Blue (430nm)" package="3 mm [THT]"]
  R2 = Resistor [tolerance=±5% resistance=220 package="0805 [SMD]"]
  R3 = Resistor [tolerance=±5% resistance=220 package="0805 [SMD]"]
  Part2 = Audio Jack Breakout
  M1 = DC Motor
  M2 = DC Motor
  Q3 = npn-Powertransistor [part_number=TIP120 package="TO220 [THT]"]
  D2 = Rectifier Diode [part_number=1N4001 package="300 mil [THT]"]
  C2 = Electrolytic Capacitor [capacitance=0.1mF package="100 mil [THT, electrolytic]"]
  M3 = DC Motor
  Q4 = npn-Powertransistor [part_number=TIP120 package="TO220 [THT]"]
  D3 = Rectifier Diode [part_number=1N4001 package="300 mil [THT]"]
  C3 = Electrolytic Capacitor [capacitance=0.1mF package="100 mil [THT, electrolytic]"]
  M4 = DC Motor
  Q5 = npn-Powertransistor [part_number=TIP120 package="TO220 [THT]"]
  D4 = Rectifier Diode [part_number=1N4001 package="300 mil [THT]"]
  C4 = Electrolytic Capacitor [capacitance=0.1mF package="100 mil [THT, electrolytic]"]

nets:
  N1: Q2.base, Part1.D5_PWM, Q3.base
  N2: Q2.collector, D1.anode, C1.+, M1.pin_1
  GND: Q2.emitter, LED1.cathode, Part1.GND, Power_plug1.GND, LED2.cathode, LED3.cathode, Part2.GND, Q3.emitter, Q4.emitter, Q5.emitter
  N3: D1.cathode, C1.-, Power_plug1.VCC, M1.pin_2, D2.cathode, C2.-, M3.pin_2, D3.cathode, C3.-, M4.pin_2, D4.cathode, C4.-
  N4: LED1.anode, R1.Pin_0
  N5: Part1.A0, Part2.TIP
  N6: Part1.ICSP_MOSI, Part1.D11_PWM/MOSI, R3.Pin_1
  N7: Part1.D9_PWM, R1.Pin_1
  N8: Part1.D10_PWM/SS, R2.Pin_1
  N9: Part1.D3_PWM, Q4.base, Q5.base
  N10: LED2.anode, R2.Pin_0
  N11: LED3.anode, R3.Pin_0
  N12: M2.pin_1, Q3.collector, D2.anode, C2.+
  N13: M3.pin_1, Q4.collector, D3.anode, C3.+
  N14: M4.pin_1, Q5.collector, D4.anode, C4.+

notes:
  To second 5V 2A power suply
  To audio source
  Vibrating motors
  VU meter LEDs
  To 5V Power suply
